# Fritzing sketch musical notes with Arduino (saved by Fritzing 0.9.3b)
breadboards: 1

parts:
  S1 = Pushbutton [package="[THT]"]
  Part1 = Arduino Uno (Rev3) - ICSP
  J1 = Piezo Speaker

nets:
  N1: S1.Pin_1, S1.Pin_2, Part1.D9_PWM
  N2: S1.Pin_3, S1.Pin_4, Part1.GND, J1.pin1
  N3: Part1.D8, J1.pin2
